// Logisim project NOR gate.circ as structural Verilog: 1 circuit, main circuit main
module main (
  input  input0,
  input  input1,
  output output0
);

  wire transistor_2_out;

  Transistor #(.\type ("n")) transistor_1 (.in(1'b0), .out(output0), .gate(input0));
  Transistor transistor_2 (.in(1'b1), .out(transistor_2_out), .gate(input0));
  Transistor transistor_3 (.in(transistor_2_out), .out(output0), .gate(input1));
  Transistor #(.\type ("n")) transistor_4 (.in(1'b0), .out(output0), .gate(input1));
endmodule
