// Logisim project Transmission gate.circ as structural Verilog: 1 circuit, main circuit main
module main (
  input  control_C0,
  input  control_C1,
  input  input0_C1,
  input  input0_C0,
  output output0_C0,
  output output0_C1
);

  wire transistor_1_out, transistor_5_out;

  Transistor transistor_1 (.in(1'b1), .out(transistor_1_out), .gate(control_C0));
  Transistor #(.\type ("n")) transistor_2 (.in(1'b0), .out(transistor_1_out), .gate(control_C0));
  Transistor transistor_3 (.in(input0_C0), .out(output0_C0), .gate(transistor_1_out));
  Transistor #(.\type ("n")) transistor_4 (.in(input0_C0), .out(output0_C0), .gate(control_C0));
  Transistor transistor_5 (.in(1'b1), .out(transistor_5_out), .gate(control_C1));
  Transistor #(.\type ("n")) transistor_6 (.in(1'b0), .out(transistor_5_out), .gate(control_C1));
  Transistor transistor_7 (.in(input0_C1), .out(output0_C1), .gate(transistor_5_out));
  Transistor #(.\type ("n")) transistor_8 (.in(input0_C1), .out(output0_C1), .gate(control_C1));
endmodule
